# Fritzing sketch Alan_prot_01 (saved by Fritzing 0.9.3b)
breadboards: 4

parts:
  Q1 = Basic FET N-Channel [part_number=IRLZ44 package="TO220 [THT]"]
  BATT-A = 18650 battery holder [package=battery-18650-kit]
  BATT-B = 18650 battery holder [package=battery-18650-kit]
  U2 = SWITCH_SPDT [package=kps-1290]
  U3 = SWITCH_SPDT [package=kps-1290]
  Skib01 = female pin header, 2 pins [form="♀ (female)"]
  R2 = Resistor [tolerance=±5% resistance=22k package=THT]  # not connected
  R3 = Resistor [tolerance=±5% resistance=22k package=THT]
  ESP32_LORA = IC, DIP package, 36 pins [chip_label=ESP32]
  R7 = Resistor [tolerance=±5% resistance=10k package=THT]
  LTV1 = LTV847 [part_number=TLP521 package="DIP (Dual Inline) [THT]"]
  R8 = Resistor [tolerance=±5% resistance=22k package=THT]
  IC2 = SO-28W [chip_label=IC package=SO(w)]
  C2 = Electrolytic Capacitor [capacitance=1000µF voltage=16V package="300 mil [THT, electrolytic]"]

nets:
  m01: Q1.gate, R3.Pin_1, ESP32_LORA.pin20
  opt01: Q1.drain, Skib01.pin2, LTV1.pin1
  GND/opt15: Q1.source, BATT-A.-, BATT-B.-, R3.Pin_0, ESP32_LORA.pin1, ESP32_LORA.pin4, ESP32_LORA.pin36, R7.Pin_0, LTV1.pin15, IC2.10, IC2.15, IC2.16, IC2.17, C2.-
  N1: BATT-A.+, U3.P
  N2: BATT-B.+, U2.P
  vcc_Bat_B: U2.S, Skib01.pin1, C2.+
  vcc_Bat_A: U3.S
  3.3V: ESP32_LORA.pin3, R8.Pin_1, IC2.9, IC2.18
  buzzer: ESP32_LORA.pin9
  opt16/senSkib01: ESP32_LORA.pin11, LTV1.pin16, R8.Pin_0
  exp_scl: ESP32_LORA.pin14, IC2.12
  exp_sda: ESP32_LORA.pin16, IC2.13
  opt02: R7.Pin_1, LTV1.pin2
  opt03: LTV1.pin3
  opt04: LTV1.pin4
  opt05: LTV1.pin5
  opt06: LTV1.pin6
  opt07: LTV1.pin7
  opt08: LTV1.pin8
  opt09: LTV1.pin9
  opt10: LTV1.pin10
  opt11: LTV1.pin11
  opt12: LTV1.pin12
  opt13: LTV1.pin13
  opt14: LTV1.pin14

notes:
  Mosfet Triggers
  Batteries
  A
  B
  A (main)
  B (skibs)
  Skibs Sensors
  Microcontroller

custom parts:
  18650 battery holder: 18650 Battery Holder
  LTV847: 4 opto-couplers
